# Fritzing sketch BluetoothWiringDiagram (saved by Fritzing 0.9.3b)

parts:
  microcontroller_ATmega328P1 = RedBot MainBoard [part_number=12097]
  BLUEFRUIT_LE1 = Adafruit Bluefruit LE UART

nets:
  N1: microcontroller_ATmega328P1.GND#159, BLUEFRUIT_LE1.MOD, BLUEFRUIT_LE1.CTS
  N2: microcontroller_ATmega328P1.RX, BLUEFRUIT_LE1.RX
  N3: microcontroller_ATmega328P1.TX, BLUEFRUIT_LE1.TX
  VDD: microcontroller_ATmega328P1.VDD, BLUEFRUIT_LE1.VIN
  N4: microcontroller_ATmega328P1.GND#163, BLUEFRUIT_LE1.RTS, BLUEFRUIT_LE1.GND

custom parts:
  RedBot MainBoard: The SparkFun RedBot Mainboard is a robotic development platform that works with the Arduino IDE. The RedBot is a motor driver and Ardiuno combination with various headers and connections, eliminating the need to stack multiple shields. By using the RedBot accessory boards and your own chassis, you can design a robot to suit your needs. The RedBot comes pre-programmed with the Optiboot (Uno)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
  Adafruit Bluefruit LE UART: Bluetooth LE UART

// code stored in the sketch: BluetoothWiringDiagram.ino

